// Logisim project experimento-3.circ as structural Verilog: 2 circuits, main circuit 1_bit_full_adder
module _1_bit_full_adder (
  input  A,
  input  B,
  input  C,
  output Sum,
  output Carry
);

  wire and_1_out, and_2_out, and_3_out, and_4_out, and_5_out, and_6_out, not_1_out, not_2_out, not_3_out,
       not_4_out, or_1_out;

  not not_1 (not_1_out, A);
  not not_2 (not_2_out, B);
  and and_1 (and_1_out, not_1_out, B);
  and and_2 (and_2_out, A, not_2_out);
  or or_1 (or_1_out, and_1_out, and_2_out);
  not not_3 (not_3_out, or_1_out);
  not not_4 (not_4_out, C);
  and and_3 (and_3_out, not_3_out, C);
  and and_4 (and_4_out, or_1_out, not_4_out);
  and and_5 (and_5_out, or_1_out, C);
  and and_6 (and_6_out, A, B);
  or or_2 (Sum, and_3_out, and_4_out);
  or or_3 (Carry, and_5_out, and_6_out);
endmodule

module _2_bit_full_adder (
  input  C,
  input  [1:0] A,
  input  [1:0] B,
  output [1:0] Sum,
  output Carry
);

  wire Full_Adder_1_bit_carry;

  _1_bit_full_adder Full_Adder_1_bit (.A(A[0]), .B(B[0]), .C(C), .Sum(Sum[0]), .Carry(Full_Adder_1_bit_carry));
  _1_bit_full_adder Full_Adder_1_bit_2 (.A(A[1]), .B(B[1]), .C(Full_Adder_1_bit_carry), .Sum(Sum[1]), .Carry(Carry));
endmodule
